# Fritzing sketch CarreraTimer (saved by Fritzing 0.8.7b)
breadboards: 2

parts:
  Bauteil1 = Arduino Uno (Rev3)
  LCD1 = LCD screen
  R1 = Photocell (LDR) [package=THT]
  R2 = Resistor [tolerance=±5% resistance=100k package=THT]
  LED1 = LED - 5mm [color="Green (560nm)" package="5 mm [THT]"]
  LED2 = LED - 5mm [color="Yellow (592nm)" package="5 mm [THT]"]
  LED3 = LED - 5mm [color="Red (635nm)" package="5 mm [THT]"]
  R3 = Resistor [tolerance=±5% resistance=220 package=THT]
  R4 = Resistor [tolerance=±5% resistance=220 package=THT]
  R5 = Resistor [tolerance=±5% resistance=220 package=THT]
  R6 = Rotary Potentiometer (Small) [maximum_resistance=100kΩ package=THT]
  S1 = Pushbutton [package=THT]
  R7 = Resistor [tolerance=±5% resistance=100k package=THT]
  R8 = Resistor [tolerance=±5% resistance=220 package=THT]
  J1 = Piezo Speaker

nets:
  N1: Bauteil1.A0, R1.pin_0, R2.Pin_1
  N2: Bauteil1.D8, R5.Pin_0
  N3: Bauteil1.D9_PWM, R4.Pin_0
  N4: Bauteil1.D10_PWM/SS, R3.Pin_0
  N5: Bauteil1.D11_PWM/MOSI, LCD1.RS
  N6: Bauteil1.D12/MISO, LCD1.E
  N7: Bauteil1.D13/SCK, S1.leg1, R7.Pin_1
  N8: Bauteil1.D2, LCD1.DB4
  N9: Bauteil1.D3_PWM, LCD1.DB5
  N10: Bauteil1.D4, LCD1.DB6
  N11: Bauteil1.D5_PWM, LCD1.DB7
  N12: Bauteil1.D6_PWM, J1.pin2
  5V: Bauteil1.5V, LCD1.VDD, R1.pin_1, R6.leg2, R7.Pin_0
  GND: Bauteil1.GND, LCD1.VSS, LCD1.R/W, R2.Pin_0, LED1.cathode, LED2.cathode, LED3.cathode, R6.leg1, S1.leg0, R8.Pin_1
  N13: LCD1.V0, R6.wiper
  N14: LED1.anode, R3.Pin_1
  N15: LED2.anode, R4.Pin_1
  N16: LED3.anode, R5.Pin_1
  N17: R8.Pin_0, J1.pin1

notes:
  FLIP FLOP
