# Fritzing sketch Countdown (saved by Fritzing 0.8.7b)
breadboards: 3

parts:
  7_Segment1 = 7 Segment Display
  Bauteil1 = Arduino Uno (Rev3)
  R1 = Resistor [tolerance=±5% resistance=2.2k package=THT]
  R2 = Resistor [tolerance=±5% resistance=2.2k package=THT]
  R3 = Resistor [tolerance=±5% resistance=4.7k package=THT]
  S1 = Pushbutton [package=THT]
  S2 = Pushbutton [package=THT]
  R4 = Resistor [tolerance=±5% resistance=100k package=THT]
  Q1 = NPN-Transistor [package="TO92 [THT]"]
  R5 = Resistor [tolerance=±5% resistance=100k package=THT]
  Q2 = Basic FET P-Channel [package="TO220 [THT]"]
  VCC2 = Battery
  VCC1 = Battery
  M1 = DC Motor

nets:
  N1: 7_Segment1.Segment_G, Bauteil1.D8
  N2: 7_Segment1.Segment_F, Bauteil1.D7
  N3: 7_Segment1.common_anode, Q1.E
  N4: 7_Segment1.Segment_E, Bauteil1.D6_PWM
  N5: 7_Segment1.Segment_D, Bauteil1.D5_PWM
  N6: 7_Segment1.Segment_DP, Bauteil1.D9_PWM
  N7: 7_Segment1.Segment_C, Bauteil1.D4
  N8: 7_Segment1.Segment_B, Bauteil1.D3_PWM
  N9: 7_Segment1.Segment_A, Bauteil1.D2
  N10: Bauteil1.D11_PWM/MOSI, Q2.gate
  N11: Bauteil1.D12/MISO, S2.leg1, R5.Pin_1
  N12: Bauteil1.D13/SCK, S1.leg1, R4.Pin_1
  N13: Bauteil1.GND, R3.Pin_1, S1.leg0, S2.leg0, Q2.source, VCC1.-
  N14: Bauteil1.5V, R1.Pin_0, R4.Pin_0, Q1.C, R5.Pin_0
  N15: R1.Pin_1, R2.Pin_0
  N16: R2.Pin_1, R3.Pin_0, Q1.B
  N17: Q2.drain, M1.pin_2
  N18: VCC2.-, VCC1.+
  N19: VCC2.+, M1.pin_1

notes:
  FLIP FLOP
