# Fritzing sketch Murmelbahn (saved by Fritzing 0.9.1b)
breadboards: 2

parts:
  Bauteil1 = Arduino Uno (Rev3)
  VCC1 = Battery block 9V
  S1 = Pushbutton [package=THT]
  S2 = Pushbutton [package=THT]
  IC1 = L293D [package=THT]
  LED1 = LED - 5mm [color="Red (633nm)" package="5 mm [THT]"]
  S3 = Pushbutton [package=THT]
  R1 = Resistor [tolerance=±5% resistance=220 package=THT]
  R2 = Resistor [tolerance=±5% resistance=220 package=THT]
  R3 = Resistor [tolerance=±5% resistance=220 package=THT]
  R4 = Resistor [tolerance=±5% resistance=220 package=THT]
  LED2 = LED - 5mm [color="Green (565nm)" package="5 mm [THT]"]
  LED3 = LED - 5mm [color="Red (633nm)" package="5 mm [THT]"]
  LED4 = LED - 5mm [color="Green (565nm)" package="5 mm [THT]"]
  R6 = Resistor [tolerance=±5% resistance=100k package=THT]
  R7 = Resistor [tolerance=±5% resistance=100k package=THT]
  R9 = Resistor [tolerance=±5% resistance=100k package=THT]
  M1 = DC Motor

nets:
  N1: Bauteil1.D8, R1.Pin_1
  N2: Bauteil1.D9_PWM, R4.Pin_1
  N3: Bauteil1.D10_PWM/SS, R3.Pin_1
  N4: Bauteil1.D11_PWM/MOSI, R2.Pin_1
  N5: Bauteil1.GND, VCC1.-, S1.leg0, S2.leg0, IC1.0V, LED1.cathode, S3.leg0, LED2.cathode, LED3.cathode, LED4.cathode
  N6: Bauteil1.D2, S3.leg1, R6.Pin_1
  N7: Bauteil1.D3_PWM, IC1.Enable_1
  N8: Bauteil1.D4, IC1.In_1
  N9: Bauteil1.D5_PWM, IC1.In_2
  N10: Bauteil1.D6_PWM, S2.leg1, R9.Pin_1
  N11: Bauteil1.D7, S1.leg1, R7.Pin_1
  N12: Bauteil1.5V, IC1.+V, R6.Pin_0, R7.Pin_0, R9.Pin_0
  N13: VCC1.+, IC1.+Vmotor
  N14: IC1.Out_1_(_Controlled_by_Enable_1_), M1.pin_1
  N15: IC1.Out_2_(_Controlled_by_Enable_1_), M1.pin_2
  N16: LED1.anode, R2.Pin_0
  N17: R1.Pin_0, LED4.anode
  N18: R3.Pin_0, LED2.anode
  N19: R4.Pin_0, LED3.anode

notes:
  FLIP FLOP
  Fischertechnik motor
  Fischertechnik battery block
  top switch
  finish switch
