# Fritzing sketch Zisternensensor (saved by Fritzing 0.9.6b)
breadboards: 1

parts:
  M1 = AJ-SR04M Module [part_number=AJ-SR04M]
  Bauteil1 = BME/BMP280
  OLED1 = OLED 128x64 I2C Monochrome Display GND-VDD
  R2 = Resistor [tolerance=±5% power=0.25 resistance=470 package=THT]
  WeMos_D1_Mini1 = WeMos D1 Mini
  Q1 = PNP-Transistor [part_number=2N3906 package="TO92 [THT]"]

nets:
  N1: M1.GND, Q1.C
  N2: M1.Echo, WeMos_D1_Mini1.D6
  N3: M1.Trig, WeMos_D1_Mini1.D5
  VCC: M1.VCC, OLED1.VDD, WeMos_D1_Mini1.5V
  N4: Bauteil1.VIN, WeMos_D1_Mini1.D1
  GND: Bauteil1.GND, OLED1.GND, WeMos_D1_Mini1.G, Q1.E
  N5: Bauteil1.SCL, OLED1.SCK, WeMos_D1_Mini1.D2
  N6: Bauteil1.SDA, OLED1.SDA, WeMos_D1_Mini1.D3
  N7: R2.Pin_0, WeMos_D1_Mini1.D8
  N8: R2.Pin_1, Q1.B
  N9: WeMos_D1_Mini1.D0, WeMos_D1_Mini1.RST

custom parts:
  AJ-SR04M Module: AJ-SR04M Ultrasonic Distance Measuring Sensor Controller Module, 3-5V DC.
  BME/BMP280: Digital temperature humidity atmospheric pressure sensor
  OLED 128x64 I2C Monochrome Display GND-VDD: OLED 128x64 I2C Monochrome Display. Note: there are two variants of this part, this one is the GND VDD SCK SDA variant. The other is VDD GND SCK SDA. Make sure you select the part that matches your module as using the incorrect part will probably destroy your module! In addition the mounting holes are marked on silkscreen but not by default drilled. If you want drilled mounting holes, copy a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
  WeMos D1 Mini: The D1 mini is a mini wifi board based on ESP-8266EX.
