# Fritzing sketch Zisternensensor_perfboard (saved by Fritzing 0.9.6b)
perfboards: 1

parts:
  M1 = AJ-SR04M Module [part_number=AJ-SR04M]
  Bauteil1 = BME/BMP280
  OLED1 = OLED 128x64 I2C Monochrome Display GND-VDD
  R2 = Resistor [tolerance=±5% power=0.25 resistance=470 package=THT]
  WeMos_D1_Mini1 = WeMos D1 Mini
  Q1 = PNP-Transistor [part_number=2N3906 package="TO92 [THT]"]
  J1 = female pin header, 8 pins [form="♀ (female)"]
  J2 = female pin header, 8 pins [form="♀ (female)"]
  J3 = female pin header, 4 pins [form="♀ (female)"]
  J4 = female pin header, 4 pins [form="♀ (female)"]
  J5 = female pin header, 4 pins [form="♀ (female)"]
  BATT1 = 4xAA Switchable Battery Pack w/Bare Wire

nets:
  N1: M1.GND, Q1.C, J5.pin1
  N2: M1.Echo, WeMos_D1_Mini1.D6, J2.pin5, J5.pin2
  N3: M1.Trig, WeMos_D1_Mini1.D5, J2.pin4, J5.pin3
  VCC: M1.VCC, OLED1.VDD, WeMos_D1_Mini1.5V, J1.pin8, J4.pin2, J5.pin4, BATT1.POS
  N4: Bauteil1.VIN, WeMos_D1_Mini1.D1, J1.pin3, J3.pin1
  GND: Bauteil1.GND, OLED1.GND, WeMos_D1_Mini1.G, Q1.E, J1.pin7, J3.pin2, J4.pin1
  N5: Bauteil1.SCL, OLED1.SCK, WeMos_D1_Mini1.D2, J1.pin4, J3.pin3, J4.pin3
  N6: Bauteil1.SDA, OLED1.SDA, WeMos_D1_Mini1.D3, J1.pin5, J3.pin4, J4.pin4
  N7: R2.Pin_0, WeMos_D1_Mini1.D8, J2.pin7
  N8: R2.Pin_1, Q1.B
  N9: WeMos_D1_Mini1.3V3, J2.pin8
  N10: WeMos_D1_Mini1.A0, J2.pin2
  N11: WeMos_D1_Mini1.D0, WeMos_D1_Mini1.RST, J2.pin1, J2.pin3
  N12: WeMos_D1_Mini1.D4, J1.pin6
  N13: WeMos_D1_Mini1.D7, J2.pin6
  N14: WeMos_D1_Mini1.RX, J1.pin2
  N15: WeMos_D1_Mini1.TX, J1.pin1

custom parts:
  AJ-SR04M Module: AJ-SR04M Ultrasonic Distance Measuring Sensor Controller Module, 3-5V DC.
  BME/BMP280: Digital temperature humidity atmospheric pressure sensor
  OLED 128x64 I2C Monochrome Display GND-VDD: OLED 128x64 I2C Monochrome Display. Note: there are two variants of this part, this one is the GND VDD SCK SDA variant. The other is VDD GND SCK SDA. Make sure you select the part that matches your module as using the incorrect part will probably destroy your module! In addition the mounting holes are marked on silkscreen but not by default drilled. If you want drilled mounting holes, copy a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
  WeMos D1 Mini: The D1 mini is a mini wifi board based on ESP-8266EX.
  4xAA Switchable Battery Pack w/Bare Wire: 4xAA Switchable Battery Pack with Bare Wire connection
